# Fritzing sketch schematic (saved by Fritzing 0.9.10b)

parts:
  esp1 = ESP32 DevKitc V4
  Componente2 = HX711 Weighing Sensor Module
  Load_Cell1 = Load Cell - Red/white/black/green
  S1 = Pushbutton [package="[THT]"]
  R1 = Resistor [tolerance=±5% power=0.25 resistance=220 package=THT]
  LCD2004-I2C1 = LCD2004-I2C

nets:
  N1: esp1.IO18, Componente2.DO/RX
  N2: esp1.IO19, Componente2.CK/TX
  N3: esp1.IO21, LCD2004-I2C1.SDA
  N4: esp1.IO22, LCD2004-I2C1.SCL
  N5: esp1.IO27, S1.Pin_3, R1.Pin_1
  GND: esp1.GND, Componente2.GND, R1.Pin_0, LCD2004-I2C1.GND
  VCC: esp1.5V, Componente2.VCC, S1.Pin_1, LCD2004-I2C1.VCC
  N6: Componente2.E+, Load_Cell1.wire1
  N7: Componente2.E-, Load_Cell1.wire3
  N8: Componente2.A+, Load_Cell1.wire2
  N9: Componente2.A-, Load_Cell1.wire4

custom parts:
  ESP32 DevKitc V4: ESP32-DevKitC board with ESP32-WROOM-32 module. ESP32-DevKitC V4 is a small-sized ESP32-based development board produced by Espressif. Most of the pins on the ESP module are broken out to the pin headers on the board. The pins D0, D1, D2, D3, CMD and CLK are used internally for communication between ESP32 and SPI flash memory. They are grouped on both sides near the USB connector. Avoid using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
  HX711 Weighing Sensor Module: HX711 is a precision 24-bit analog-to-digital converter (ADC) designed for weigh scales and industrial control applications to interface directly with a bridge sensor.
  Load Cell - Red/white/black/green: A rectangle load cell/weighting pressure Sensor with four wires - Red, white, black, green. Normally corresponding with E+, E-, A+, A- respectively.
  LCD2004-I2C: A standard character display with 4x20 characters. Comes in many colors with LCM2004 IIC attached.
